// Logisim project alu.circ as structural Verilog: 1 circuit, main circuit alu
module alu (
  input  [31:0] A,
  input  [31:0] B,
  input  [3:0] ALUSel,
  output [31:0] ALUResult
);

  wire comparator_1_lt;
  wire [4:0] bitselector_1_out, bitselector_2_out, bitselector_3_out;
  wire [31:0] add0, AND_out, mul, mulh, mulhu, OR_Out, SLLS, slt, SRAS, SRU, sub, XOR_OUTPUT;

  BitSelector #(.group(5), .width(32)) bitselector_1 (.in(B), .out(bitselector_1_out), .sel(3'b000));
  BitSelector #(.group(5), .width(32)) bitselector_2 (.in(B), .out(bitselector_2_out), .sel(3'b000));
  assign XOR_OUTPUT = A ^ B;  // XOR_Gate xor_1, 32 bits wide
  Shifter #(.shift("lr"), .width(32)) shifter_1 (.in(A), .\dist (bitselector_2_out), .out(SRU));
  Shifter #(.width(32)) shifter_2 (.in(A), .\dist (bitselector_1_out), .out(SLLS));
  Adder #(.width(32)) adder_1 (.a(A), .b(B), .out(add0));  // open: cin, cout
  assign OR_Out = A | B;  // OR_Gate or_1, 32 bits wide
  assign AND_out = A & B;  // AND_Gate and_1, 32 bits wide
  Multiplier #(.mode("twosComplement"), .width(32)) multiplier_1 (.a(A), .b(B), .out(mul), .cout(mulh));  // open: cin
  Multiplier #(.width(32)) multiplier_2 (.a(A), .b(B), .cout(mulhu));  // open: out, cin
  BitSelector #(.group(5), .width(32)) bitselector_3 (.in(B), .out(bitselector_3_out), .sel(3'b000));
  Shifter #(.shift("ar"), .width(32)) shifter_3 (.in(A), .\dist (bitselector_3_out), .out(SRAS));
  Multiplexer #(.select(4), .width(32)) multiplexer_1 (
    .in0(add0), .in1(SLLS), .in2(slt), .in4(XOR_OUTPUT), .in5(SRU), .in6(OR_Out), .in7(AND_out), .in8(mul),
    .in9(mulh), .in11(mulhu), .in12(sub), .in13(SRAS), .in15(B), .out(ALUResult), .sel(ALUSel));  // open: in3, in10, in14
  Subtractor #(.width(32)) subtractor_1 (.a(A), .b(B), .out(sub));  // open: bin, bout
  Comparator #(.width(32)) comparator_1 (.a(A), .b(B), .lt(comparator_1_lt));  // open: gt, eq
  assign slt = {{31{1'b0}}, comparator_1_lt};  // Bit_Extender bit_extender_1

  // Notes on the sheet:
  //   INPUTS to your circuit
  //   DON'T CHANGE THE LOCATIONS OF THE INPUTS AND OUTPUTS!
  //   OUTPUT from your circuit
endmodule
