// Logisim project control-logic.circ as structural Verilog: 1 circuit, main circuit control_logic
module control_logic (
  input  [31:0] inst,
  input  BrEq,
  input  BrLt,
  output PCSel,
  output RegWEn,
  output [2:0] ImmSel,
  output BrUn,
  output ASel,
  output BSel,
  output [3:0] ALUSel,
  output MemRW,
  output [1:0] WBSel,
  output CSRSel,
  output CSRWen
);

  wire add, addi, alu_and, alu_mul, alu_mulh, alu_mulhu, alu_or, alu_sll, alu_slt, alu_sra, alu_srl, alu_sub,
       alu_xor, and1, and_1_out, and_2_out, and_3_out, and_4_out, and_5_out, and_6_out, and_7_out, and_8_out,
       and_9_out, and_10_out, and_11_out, and_12_out, and_13_out, and_14_out, and_15_out, and_28_out,
       and_30_out, and_32_out, and_34_out, and_36_out, and_37_out, and_38_out, and_40_out, and_42_out,
       and_43_out, and_44_out, and_46_out, and_48_out, and_49_out, and_50_out, and_57_out, and_58_out,
       and_59_out, and_60_out, and_62_out, and_66_out, and_67_out, and_70_out, and_71_out, and_72_out,
       and_73_out, and_74_out, andi, auipc, beq, bge, bgeu, blt, bltu, bne, comparator_11_eq,
       comparator_12_eq, comparator_13_eq, comparator_14_eq, comparator_15_eq, comparator_16_eq,
       comparator_17_eq, comparator_18_eq, comparator_19_eq, comparator_20_eq, comparator_21_eq,
       comparator_22_eq, comparator_23_eq, comparator_24_eq, comparator_25_eq, comparator_26_eq,
       comparator_27_eq, comparator_28_eq, comparator_29_eq, comparator_30_eq, comparator_31_eq,
       comparator_32_eq, comparator_33_eq, comparator_34_eq, comparator_35_eq, comparator_36_eq,
       comparator_37_eq, comparator_38_eq, comparator_39_eq, comparator_40_eq, comparator_41_eq,
       comparator_42_eq, comparator_43_eq, comparator_44_eq, comparator_45_eq, comparator_46_eq,
       comparator_47_eq, comparator_48_eq, comparator_49_eq, comparator_50_eq, comparator_51_eq,
       comparator_52_eq, comparator_53_eq, comparator_54_eq, comparator_55_eq, comparator_56_eq,
       comparator_57_eq, csrw, I_type_csr, I_type_imm, I_type_jal, I_type_load, jal, jalr, lb, lh, lui, lw,
       not_1_out, not_2_out, not_3_out, or1, or_12_out, or_13_out, or_14_out, or_15_out, or_17_out,
       or_24_out, ori, R_type, sb, SB_type, sh, sll1, slli, slt, slti, sra1, srai, srl1, srli, sw,
       U_type_imm, U_type_pc, xor1, xori;
  wire [1:0] bit_extender_1_out, bit_extender_2_out, wbsel_mem_load, wbsel_pc4_wb;

  Comparator #(.width(7)) comparator_1 (.a(inst[6:0]), .b(7'b0110011), .eq(R_type));  // open: gt, lt
  Comparator #(.width(7)) comparator_2 (.a(inst[6:0]), .b(7'b0000011), .eq(I_type_load));  // open: gt, lt
  Comparator #(.width(7)) comparator_3 (.a(inst[6:0]), .b(7'b0010011), .eq(I_type_imm));  // open: gt, lt
  Comparator #(.width(7)) comparator_4 (.a(inst[6:0]), .b(7'b0100011), .eq(MemRW));  // open: gt, lt
  Comparator #(.width(7)) comparator_5 (.a(inst[6:0]), .b(7'b1100011), .eq(SB_type));  // open: gt, lt
  Comparator #(.width(7)) comparator_6 (.a(inst[6:0]), .b(7'b0010111), .eq(U_type_pc));  // open: gt, lt
  Comparator #(.width(7)) comparator_7 (.a(inst[6:0]), .b(7'b0110111), .eq(U_type_imm));  // open: gt, lt
  Comparator #(.width(7)) comparator_8 (.a(inst[6:0]), .b(7'b1101111), .eq(ImmSel[2]));  // open: gt, lt
  Comparator #(.width(7)) comparator_9 (.a(inst[6:0]), .b(7'b1100111), .eq(I_type_jal));  // open: gt, lt
  Comparator #(.width(7)) comparator_10 (.a(inst[6:0]), .b(7'b1110011), .eq(I_type_csr));  // open: gt, lt
  or or_1 (alu_slt, slt, slti);
  or or_2 (alu_srl, srl1, srli);
  or or_3 (alu_sra, sra1, srai);
  or or_4 (alu_or, or1, ori);
  or or_5 (alu_sll, sll1, slli);
  or or_6 (alu_and, and1, andi);
  or or_7 (alu_xor, xor1, xori);
  and and_1 (and_1_out, R_type, 1'b1);
  Comparator #(.width(3)) comparator_11 (.a(inst[14:12]), .b(3'b000), .eq(comparator_11_eq));  // open: gt, lt
  and and_2 (and_2_out, R_type, 1'b1);
  Comparator #(.width(3)) comparator_12 (.a(inst[14:12]), .b(3'b001), .eq(comparator_12_eq));  // open: gt, lt
  and and_3 (and_3_out, R_type, 1'b1);
  Comparator #(.width(3)) comparator_13 (.a(inst[14:12]), .b(3'b011), .eq(comparator_13_eq));  // open: gt, lt
  Comparator #(.width(3)) comparator_14 (.a(inst[14:12]), .b(3'b010), .eq(comparator_14_eq));  // open: gt, lt
  and and_4 (and_4_out, R_type, 1'b1);
  Comparator #(.width(3)) comparator_15 (.a(inst[14:12]), .b(3'b100), .eq(comparator_15_eq));  // open: gt, lt
  and and_5 (and_5_out, R_type, 1'b1);
  Comparator #(.width(3)) comparator_16 (.a(inst[14:12]), .b(3'b101), .eq(comparator_16_eq));  // open: gt, lt
  and and_6 (and_6_out, R_type, 1'b1);
  Comparator #(.width(3)) comparator_17 (.a(inst[14:12]), .b(3'b110), .eq(comparator_17_eq));  // open: gt, lt
  and and_7 (and_7_out, R_type, 1'b1);
  Comparator #(.width(3)) comparator_18 (.a(inst[14:12]), .b(3'b111), .eq(comparator_18_eq));  // open: gt, lt
  and and_8 (and_8_out, and_1_out, comparator_11_eq);
  and and_9 (and_9_out, and_2_out, comparator_12_eq);
  and and_10 (and_10_out, and_3_out, comparator_13_eq);
  and and_11 (and_11_out, R_type, comparator_14_eq);
  and and_12 (and_12_out, and_4_out, comparator_15_eq);
  and and_13 (and_13_out, and_5_out, comparator_16_eq);
  and and_14 (and_14_out, and_6_out, comparator_17_eq);
  and and_15 (and_15_out, and_7_out, comparator_18_eq);
  Comparator #(.width(7)) comparator_19 (.a(inst[31:25]), .b({7{1'b0}}), .eq(comparator_19_eq));  // open: gt, lt
  Comparator #(.width(7)) comparator_20 (.a(inst[31:25]), .b(7'b0000001), .eq(comparator_20_eq));  // open: gt, lt
  Comparator #(.width(7)) comparator_21 (.a(inst[31:25]), .b(7'b0100000), .eq(comparator_21_eq));  // open: gt, lt
  Comparator #(.width(7)) comparator_22 (.a(inst[31:25]), .b({7{1'b0}}), .eq(comparator_22_eq));  // open: gt, lt
  Comparator #(.width(7)) comparator_23 (.a(inst[31:25]), .b(7'b0000001), .eq(comparator_23_eq));  // open: gt, lt
  Comparator #(.width(7)) comparator_24 (.a(inst[31:25]), .b(7'b0000001), .eq(comparator_24_eq));  // open: gt, lt
  Comparator #(.width(7)) comparator_25 (.a(inst[31:25]), .b({7{1'b0}}), .eq(comparator_25_eq));  // open: gt, lt
  Comparator #(.width(7)) comparator_26 (.a(inst[31:25]), .b({7{1'b0}}), .eq(comparator_26_eq));  // open: gt, lt
  Comparator #(.width(7)) comparator_27 (.a(inst[31:25]), .b({7{1'b0}}), .eq(comparator_27_eq));  // open: gt, lt
  Comparator #(.width(7)) comparator_28 (.a(inst[31:25]), .b(7'b0100000), .eq(comparator_28_eq));  // open: gt, lt
  Comparator #(.width(7)) comparator_29 (.a(inst[31:25]), .b({7{1'b0}}), .eq(comparator_29_eq));  // open: gt, lt
  Comparator #(.width(7)) comparator_30 (.a(inst[31:25]), .b({7{1'b0}}), .eq(comparator_30_eq));  // open: gt, lt
  or or_8 (ALUSel[0], alu_sll, alu_srl, alu_and, alu_mulh, alu_mulhu, alu_sra, lui);
  or or_9 (ALUSel[1], alu_slt, alu_or, alu_and, alu_mulhu, lui);
  or or_10 (ALUSel[2], alu_xor, alu_srl, alu_or, alu_and, alu_sub, alu_sra, lui);
  or or_11 (ALUSel[3], alu_mul, alu_mulh, alu_mulhu, alu_sub, alu_sra, lui);
  and and_16 (add, and_8_out, comparator_19_eq);
  and and_17 (alu_mul, and_8_out, comparator_20_eq);
  and and_18 (alu_sub, and_8_out, comparator_21_eq);
  and and_19 (sll1, and_9_out, comparator_22_eq);
  and and_20 (alu_mulh, and_9_out, comparator_23_eq);
  and and_21 (alu_mulhu, and_10_out, comparator_24_eq);
  and and_22 (slt, and_11_out, comparator_25_eq);
  and and_23 (xor1, and_12_out, comparator_26_eq);
  and and_24 (srl1, and_13_out, comparator_27_eq);
  and and_25 (sra1, and_13_out, comparator_28_eq);
  and and_26 (or1, and_14_out, comparator_29_eq);
  and and_27 (and1, and_15_out, comparator_30_eq);
  Comparator #(.width(3)) comparator_31 (.a(inst[14:12]), .b(3'b000), .eq(comparator_31_eq));  // open: gt, lt
  Comparator #(.width(3)) comparator_32 (.a(inst[14:12]), .b(3'b001), .eq(comparator_32_eq));  // open: gt, lt
  Comparator #(.width(3)) comparator_33 (.a(inst[14:12]), .b(3'b010), .eq(comparator_33_eq));  // open: gt, lt
  Comparator #(.width(3)) comparator_34 (.a(inst[14:12]), .b(3'b000), .eq(comparator_34_eq));  // open: gt, lt
  Comparator #(.width(3)) comparator_35 (.a(inst[14:12]), .b(3'b001), .eq(comparator_35_eq));  // open: gt, lt
  Comparator #(.width(3)) comparator_36 (.a(inst[14:12]), .b(3'b010), .eq(comparator_36_eq));  // open: gt, lt
  Comparator #(.width(3)) comparator_37 (.a(inst[14:12]), .b(3'b100), .eq(comparator_37_eq));  // open: gt, lt
  Comparator #(.width(3)) comparator_38 (.a(inst[14:12]), .b(3'b101), .eq(comparator_38_eq));  // open: gt, lt
  Comparator #(.width(3)) comparator_39 (.a(inst[14:12]), .b(3'b110), .eq(comparator_39_eq));  // open: gt, lt
  Comparator #(.width(3)) comparator_40 (.a(inst[14:12]), .b(3'b111), .eq(comparator_40_eq));  // open: gt, lt
  and and_28 (and_28_out, I_type_load, 1'b1);
  and and_29 (lb, and_28_out, comparator_31_eq);
  and and_30 (and_30_out, I_type_load, 1'b1);
  and and_31 (lh, and_30_out, comparator_32_eq);
  and and_32 (and_32_out, I_type_load, 1'b1);
  and and_33 (lw, and_32_out, comparator_33_eq);
  and and_34 (and_34_out, I_type_imm, 1'b1);
  and and_35 (addi, and_34_out, comparator_34_eq);
  and and_36 (and_36_out, I_type_imm, 1'b1);
  and and_37 (and_37_out, and_36_out, comparator_35_eq);
  and and_38 (and_38_out, I_type_imm, 1'b1);
  and and_39 (slti, and_38_out, comparator_36_eq);
  and and_40 (and_40_out, I_type_imm, 1'b1);
  and and_41 (xori, and_40_out, comparator_37_eq);
  and and_42 (and_42_out, I_type_imm, 1'b1);
  and and_43 (and_43_out, and_42_out, comparator_38_eq);
  and and_44 (and_44_out, I_type_imm, 1'b1);
  and and_45 (ori, and_44_out, comparator_39_eq);
  and and_46 (and_46_out, I_type_imm, 1'b1);
  and and_47 (andi, and_46_out, comparator_40_eq);
  Comparator #(.width(7)) comparator_41 (.a(inst[31:25]), .b({7{1'b0}}), .eq(comparator_41_eq));  // open: gt, lt
  Comparator #(.width(7)) comparator_42 (.a(inst[31:25]), .b({7{1'b0}}), .eq(comparator_42_eq));  // open: gt, lt
  Comparator #(.width(7)) comparator_43 (.a(inst[31:25]), .b(7'b0100000), .eq(comparator_43_eq));  // open: gt, lt
  and and_48 (and_48_out, MemRW, 1'b1);
  Comparator #(.width(3)) comparator_44 (.a(inst[14:12]), .b(3'b000), .eq(comparator_44_eq));  // open: gt, lt
  and and_49 (and_49_out, MemRW, 1'b1);
  Comparator #(.width(3)) comparator_45 (.a(inst[14:12]), .b(3'b001), .eq(comparator_45_eq));  // open: gt, lt
  and and_50 (and_50_out, MemRW, 1'b1);
  Comparator #(.width(3)) comparator_46 (.a(inst[14:12]), .b(3'b010), .eq(comparator_46_eq));  // open: gt, lt
  and and_51 (slli, and_37_out, comparator_41_eq);
  and and_52 (srli, and_43_out, comparator_42_eq);
  and and_53 (srai, and_43_out, comparator_43_eq);
  and and_54 (sb, and_48_out, comparator_44_eq);
  and and_55 (sh, and_49_out, comparator_45_eq);
  and and_56 (sw, and_50_out, comparator_46_eq);
  Comparator #(.width(3)) comparator_47 (.a(inst[14:12]), .b(3'b000), .eq(comparator_47_eq));  // open: gt, lt
  or or_12 (or_12_out, bge, bgeu);
  or or_13 (or_13_out, blt, bltu);
  or or_14 (or_14_out, lb, lh, lw);
  and and_57 (and_57_out, SB_type, 1'b1);
  Comparator #(.width(3)) comparator_48 (.a(inst[14:12]), .b(3'b000), .eq(comparator_48_eq));  // open: gt, lt
  and and_58 (and_58_out, SB_type, 1'b1);
  Comparator #(.width(3)) comparator_49 (.a(inst[14:12]), .b(3'b001), .eq(comparator_49_eq));  // open: gt, lt
  and and_59 (and_59_out, SB_type, 1'b1);
  Comparator #(.width(3)) comparator_50 (.a(inst[14:12]), .b(3'b100), .eq(comparator_50_eq));  // open: gt, lt
  and and_60 (and_60_out, I_type_jal, 1'b1);
  and and_61 (jalr, and_60_out, comparator_47_eq);
  not not_1 (not_1_out, BrLt);
  and and_62 (and_62_out, beq, BrEq);
  assign bit_extender_1_out = {{1{or_14_out}}, or_14_out};  // Bit_Extender bit_extender_1
  assign bit_extender_2_out = {{1{or_15_out}}, or_15_out};  // Bit_Extender bit_extender_2
  or or_15 (or_15_out, jalr, ImmSel[2]);
  and and_63 (beq, and_57_out, comparator_48_eq);
  and and_64 (bne, and_58_out, comparator_49_eq);
  and and_65 (blt, and_59_out, comparator_50_eq);
  and and_66 (and_66_out, or_12_out, not_1_out);
  and and_67 (and_67_out, or_13_out, BrLt);
  or or_16 (ImmSel[1], SB_type, U_type_pc, U_type_imm);
  assign wbsel_mem_load = 2'b01 & bit_extender_1_out;  // AND_Gate and_68, 2 bits wide
  assign wbsel_pc4_wb = 2'b10 & bit_extender_2_out;  // AND_Gate and_69, 2 bits wide
  not not_2 (not_2_out, BrEq);
  or or_17 (or_17_out, R_type, U_type_pc, I_type_load, I_type_imm, U_type_imm, ImmSel[2], I_type_jal, I_type_csr);
  or or_18 (ImmSel[0], MemRW, U_type_pc, U_type_imm);
  and and_70 (and_70_out, bne, not_2_out);
  and and_71 (and_71_out, SB_type, 1'b1);
  Comparator #(.width(3)) comparator_51 (.a(inst[14:12]), .b(3'b101), .eq(comparator_51_eq));  // open: gt, lt
  and and_72 (and_72_out, SB_type, 1'b1);
  Comparator #(.width(3)) comparator_52 (.a(inst[14:12]), .b(3'b110), .eq(comparator_52_eq));  // open: gt, lt
  and and_73 (and_73_out, SB_type, 1'b1);
  Comparator #(.width(3)) comparator_53 (.a(inst[14:12]), .b(3'b111), .eq(comparator_53_eq));  // open: gt, lt
  and and_74 (and_74_out, I_type_csr, 1'b1);
  or or_19 (PCSel, and_66_out, and_62_out, and_67_out, jalr, ImmSel[2], and_70_out);
  and and_75 (RegWEn, or_17_out, not_3_out);
  not not_3 (not_3_out, CSRWen);
  and and_76 (bge, and_71_out, comparator_51_eq);
  and and_77 (bltu, and_72_out, comparator_52_eq);
  and and_78 (bgeu, and_73_out, comparator_53_eq);
  and and_79 (csrw, and_74_out, comparator_54_eq);
  Comparator #(.width(3)) comparator_54 (.a(inst[14:12]), .b(3'b001), .eq(comparator_54_eq));  // open: gt, lt
  and and_80 (CSRSel, and_74_out, comparator_55_eq);
  Comparator #(.width(3)) comparator_55 (.a(inst[14:12]), .b(3'b101), .eq(comparator_55_eq));  // open: gt, lt
  assign WBSel = wbsel_pc4_wb | wbsel_mem_load;  // OR_Gate or_20, 2 bits wide
  or or_21 (CSRWen, csrw, CSRSel);
  and and_81 (auipc, U_type_pc, 1'b1);
  and and_82 (lui, U_type_imm, 1'b1);
  and and_83 (jal, ImmSel[2], 1'b1);
  or or_22 (ASel, SB_type, ImmSel[2], U_type_imm, U_type_pc);
  or or_23 (BSel, SB_type, MemRW, U_type_pc, U_type_imm, I_type_csr, I_type_jal, ImmSel[2], I_type_load, I_type_imm);
  Comparator #(.width(3)) comparator_56 (.a(inst[14:12]), .b(3'b110), .eq(comparator_56_eq));  // open: gt, lt
  Comparator #(.width(3)) comparator_57 (.a(inst[14:12]), .b(3'b111), .eq(comparator_57_eq));  // open: gt, lt
  or or_24 (or_24_out, comparator_56_eq, comparator_57_eq);
  and and_84 (BrUn, or_24_out, SB_type);

  // Other names for the same wires on the sheet: csrwi = CSRSel; UJ_type = ImmSel[2]; opcode[6:0] = inst[6:0];
  //   rd[4:0] = inst[11:7]; funct3[2:0] = inst[14:12]; funct7[6:0] = inst[31:25]; mul = alu_mul; mulh = alu_mulh;
  //   mulhu = alu_mulhu; S_type = MemRW; sub = alu_sub

  // Notes on the sheet:
  //   INPUTS to your circuit
  //   DON'T CHANGE THE LOCATIONS OF THE INPUTS AND OUTPUTS!
  //   OUTPUT from your circuit
endmodule
