// Logisim project cpu.circ as structural Verilog: 1 circuit, main circuit cpu
module cpu (
  input  clk,
  input  [31:0] INSTRUCTION,
  input  [31:0] READ_DATA,
  output [31:0] WRITE_ADDRESS,
  output [31:0] PROGRAM_COUNTER,
  output [31:0] ra,
  output [31:0] sp,
  output [31:0] t0,
  output [31:0] t1,
  output [31:0] t2,
  output [31:0] s0,
  output [31:0] s1,
  output [31:0] a0,
  output [31:0] tohost,
  output [3:0] WRITE_ENABLE,
  output [31:0] WRITE_DATA
);

  wire ASel, BrEq, BrLt, BrUn, BSel, comparator_1_eq, comparator_2_eq, comparator_3_eq, CSRSel, CSRWen,
       MemRW, PCSel, RegWEn;
  wire [1:0] WBSel;
  wire [2:0] funct3, ImmSel;
  wire [3:0] ALUSel, multiplexer_4_out, shifter_1_out, shifter_2_out;
  wire [4:0] bit_extender_2_out, multiplier_1_out;
  wire [7:0] and_1_out, bit_extender_3_out;
  wire [11:0] CSRAdd;
  wire [15:0] and_2_out, bit_extender_4_out;
  wire [19:0] INST;
  wire [31:0] adder_1_out, adder_2_out, aluA, aluB, and_3_out, bit_extender_1_out, bit_extender_5_out,
       bit_extender_6_out, bit_extender_7_out, bit_extender_8_out, CSRDin, imm, mem_load, multiplexer_1_out,
       multiplexer_3_out, PC, rd1, rd2, shifter_4_out, shifter_5_out, shifter_6_out, wb;

  Adder #(.width(32)) adder_1 (.a(PROGRAM_COUNTER), .b(32'h4), .out(adder_1_out));  // open: cin, cout
  assign bit_extender_1_out = {{27{INST[19]}}, INST[19:15]};  // Bit_Extender bit_extender_1
  Register #(.width(32)) u_PC (.D(multiplexer_1_out), .clk(clk), .Q(PROGRAM_COUNTER));  // open: en, clr
  Multiplexer #(.enable("false"), .width(32)) multiplexer_1 (
    .in0(adder_1_out), .in1(WRITE_ADDRESS), .out(multiplexer_1_out), .sel(PCSel));
  Multiplexer #(.enable("false"), .width(32)) multiplexer_2 (
    .in0(rd1), .in1(bit_extender_1_out), .out(CSRDin), .sel(CSRSel));
  Shifter #(.width(4)) shifter_1 (.in(4'b0001), .\dist (WRITE_ADDRESS[1:0]), .out(shifter_1_out));
  Shifter #(.width(4)) shifter_2 (.in(4'b0011), .\dist (WRITE_ADDRESS[1:0]), .out(shifter_2_out));
  assign bit_extender_2_out = {{3{1'b0}}, WRITE_ADDRESS[1:0]};  // Bit_Extender bit_extender_2
  imm_gen imm_gen_1 (.Instruction({CSRAdd, INST[19:15], funct3, INST[11:0]}), .ImmSel(ImmSel), .Immediate(imm));
  Multiplier #(.width(5)) multiplier_1 (
    .a(bit_extender_2_out), .b(5'b01000), .out(multiplier_1_out));  // open: cin, cout
  Register #(.width(32)) register_1 (.D(PROGRAM_COUNTER), .clk(clk), .Q(PC));  // open: en, clr
  Multiplexer #(.enable("false"), .width(32)) multiplexer_3 (
    .in0(INSTRUCTION), .in1(32'h13), .out(multiplexer_3_out), .sel(PCSel));
  // control_logic control_logic_1: pin names not known; wires that end beside it: {CSRAdd, INST[19:15], funct3, INST[11:0]}, PCSel, RegWEn, ImmSel, BrEq, BrLt, BrUn, ASel, BSel, ALUSel, MemRW, WBSel, CSRSel, CSRWen
  Register #(.width(32)) register_2 (
    .D(multiplexer_3_out), .clk(clk), .Q({CSRAdd, INST[19:15], funct3, INST[11:0]}));  // open: en, clr
  Shifter #(.width(32)) shifter_3 (.in(rd2), .\dist (multiplier_1_out), .out(WRITE_DATA));
  Shifter #(.shift("lr"), .width(32)) shifter_4 (.in(READ_DATA), .\dist (multiplier_1_out), .out(shifter_4_out));
  Comparator #(.width(3)) comparator_1 (.a(funct3), .b(3'b000), .eq(comparator_1_eq));  // open: gt, lt
  Shifter #(.shift("lr"), .width(32)) shifter_5 (.in(READ_DATA), .\dist (multiplier_1_out), .out(shifter_5_out));
  Comparator #(.width(3)) comparator_2 (.a(funct3), .b(3'b001), .eq(comparator_2_eq));  // open: gt, lt
  Shifter #(.shift("lr"), .width(32)) shifter_6 (.in(READ_DATA), .\dist (multiplier_1_out), .out(shifter_6_out));
  Comparator #(.width(3)) comparator_3 (.a(funct3), .b(3'b010), .eq(comparator_3_eq));  // open: gt, lt
  Multiplexer #(.enable("false"), .select(3), .width(4)) multiplexer_4 (
    .in0(shifter_1_out), .in1(shifter_2_out), .in2(4'b1111), .out(multiplexer_4_out), .sel(funct3));  // open: in3, in4, in5, in6, in7
  assign and_1_out = shifter_4_out[7:0] & bit_extender_3_out;  // AND_Gate and_1, 8 bits wide
  assign bit_extender_3_out = {{7{comparator_1_eq}}, comparator_1_eq};  // Bit_Extender bit_extender_3
  assign and_2_out = shifter_5_out[15:0] & bit_extender_4_out;  // AND_Gate and_2, 16 bits wide
  assign bit_extender_4_out = {{15{comparator_2_eq}}, comparator_2_eq};  // Bit_Extender bit_extender_4
  assign and_3_out = shifter_6_out & bit_extender_5_out;  // AND_Gate and_3, 32 bits wide
  assign bit_extender_5_out = {{31{comparator_3_eq}}, comparator_3_eq};  // Bit_Extender bit_extender_5
  assign bit_extender_6_out = {{24{and_1_out[7]}}, and_1_out};  // Bit_Extender bit_extender_6
  assign bit_extender_7_out = {{16{and_2_out[15]}}, and_2_out};  // Bit_Extender bit_extender_7
  Bit_Extender #(.in_width(32), .out_width(32)) bit_extender_8 (.in(and_3_out), .out(bit_extender_8_out));
  regfile regfile_1 (
    .rs1(INST[19:15]), .rs2(CSRAdd[4:0]), .rd(INST[11:7]), .Write_Data(wb), .RegWEn(RegWEn), .clk(clk),
    .ra(ra), .sp(sp), .t0(t0), .t1(t1), .t2(t2), .s0(s0), .s1(s1), .a0(a0), .Read_Data_1(rd1),
    .Read_Data_2(rd2));
  Adder #(.width(32)) adder_2 (.a(32'h4), .b(PC), .out(adder_2_out));  // open: cin, cout
  branch_comp branch_comp_1 (.BrData1(rd1), .BrData2(rd2), .BrUn(BrUn), .BrEq(BrEq), .BrLt(BrLt));
  Multiplexer #(.enable("false"), .width(4)) multiplexer_5 (
    .in0(4'b0000), .in1(multiplexer_4_out), .out(WRITE_ENABLE), .sel(MemRW));
  Multiplexer #(.enable("false"), .select(2), .width(32)) multiplexer_6 (
    .in0(WRITE_ADDRESS), .in1(mem_load), .in2(adder_2_out), .out(wb), .sel(WBSel));  // open: in3
  assign mem_load = bit_extender_6_out | bit_extender_7_out | bit_extender_8_out;  // OR_Gate or_1, 32 bits wide
  alu alu_1 (.A(aluA), .B(aluB), .ALUSel(ALUSel), .ALUResult(WRITE_ADDRESS));
  Multiplexer #(.enable("false"), .width(32)) multiplexer_7 (.in0(rd1), .in1(PC), .out(aluA), .sel(ASel));
  Multiplexer #(.enable("false"), .width(32)) multiplexer_8 (.in0(rd2), .in1(imm), .out(aluB), .sel(BSel));
  // csr csr_1: pin names not known; wires that end beside it: CSRAdd, CSRDin, CSRWen, clk, tohost

  // Other names for the same wires on the sheet: opcode[6:0] = INST[6:0]; rd[4:0] = INST[11:7];
  //   INST (some bits) = {CSRAdd, funct3}; rs1[4:0] = INST[19:15]; rs2[4:0] = CSRAdd[4:0]; funct7[6:0] = CSRAdd[11:5]

  // Notes on the sheet:
  //   Output to IMEM
  //   IMEM (do **NOT** move this)
  //   Inputs from IMEM
  //   It is OK to move the PC, RegFile, ALU, MEM, Branch Comp, Imm Gen, and Control Logic to wherever is most convenient for you when constructing your CPU, and to delete this text
  //   Inputs/Outputs for testing. Do **NOT** move these.
  //   Outputs To DMEM
  //   DMEM (do **NOT** move this)
  //   Inputs From DMEM
endmodule
