// Logisim project imm-gen.circ as structural Verilog: 1 circuit, main circuit imm_gen
module imm_gen (
  input  [31:0] Instruction,
  input  [2:0] ImmSel,
  output [31:0] Immediate
);

  wire comparator_1_eq, comparator_2_eq, comparator_3_eq, comparator_4_eq, comparator_5_eq, comparator_6_eq,
       comparator_7_eq, comparator_8_eq, or_1_out;
  wire [12:0] bit_extender_2_out, shifter_3_out;
  wire [31:0] demultiplexer_1_out1, demultiplexer_2_out1, demultiplexer_3_out1, demultiplexer_4_out1,
       demultiplexer_5_out0, demultiplexer_5_out1;

  Comparator #(.width(7)) comparator_1 (.a(Instruction[6:0]), .b(7'b0010011), .eq(comparator_1_eq));  // open: gt, lt
  Comparator #(.width(7)) comparator_2 (.a(Instruction[6:0]), .b(7'b0000011), .eq(comparator_2_eq));  // open: gt, lt
  Comparator #(.width(7)) comparator_3 (.a(Instruction[6:0]), .b(7'b0100011), .eq(comparator_3_eq));  // open: gt, lt
  Shifter #(.shift("ar"), .width(32)) shifter_1 (.in(Instruction), .\dist (5'b10100), .out(Immediate));
  Demultiplexer #(.width(32)) demultiplexer_1 (
    .out1(demultiplexer_1_out1), .in(Instruction), .sel(comparator_1_eq));  // open: out0
  Comparator #(.width(7)) comparator_4 (.a(Instruction[6:0]), .b(7'b1100011), .eq(comparator_4_eq));  // open: gt, lt
  Comparator #(.width(7)) comparator_5 (.a(Instruction[6:0]), .b(7'b1101111), .eq(comparator_5_eq));  // open: gt, lt
  Demultiplexer #(.width(32)) demultiplexer_2 (
    .out1(demultiplexer_2_out1), .in(Instruction), .sel(comparator_2_eq));  // open: out0
  Demultiplexer #(.width(32)) demultiplexer_3 (
    .out1(demultiplexer_3_out1), .in(Instruction), .sel(comparator_3_eq));  // open: out0
  Demultiplexer #(.width(32)) demultiplexer_4 (
    .out1(demultiplexer_4_out1), .in(Instruction), .sel(comparator_4_eq));  // open: out0
  Comparator #(.width(3)) comparator_6 (
    .a(demultiplexer_1_out1[14:12]), .b(3'b001), .eq(comparator_6_eq));  // open: gt, lt
  Comparator #(.width(3)) comparator_7 (
    .a(demultiplexer_1_out1[14:12]), .b(3'b101), .eq(comparator_7_eq));  // open: gt, lt
  Shifter #(.shift("ar"), .width(32)) shifter_2 (.in(demultiplexer_2_out1), .\dist (5'b10100), .out(Immediate));
  or or_1 (or_1_out, comparator_6_eq, comparator_7_eq);
  assign Immediate = {{20{demultiplexer_3_out1[31]}}, {demultiplexer_3_out1[31:25], demultiplexer_3_out1[11:7]}};  // Bit_Extender bit_extender_1
  assign bit_extender_2_out = {{1{1'b0}}, {demultiplexer_4_out1[31], demultiplexer_4_out1[7], demultiplexer_4_out1[30:25], demultiplexer_4_out1[11:8]}};  // Bit_Extender bit_extender_2
  Comparator #(.width(1)) comparator_8 (.a(or_1_out), .b(1'b1), .eq(comparator_8_eq));  // open: gt, lt
  Shifter #(.width(13)) shifter_3 (.in(bit_extender_2_out), .\dist (4'b0001), .out(shifter_3_out));
  assign Immediate = {{19{shifter_3_out[12]}}, shifter_3_out};  // Bit_Extender bit_extender_3
  Demultiplexer #(.width(32)) demultiplexer_5 (
    .out0(demultiplexer_5_out0), .out1(demultiplexer_5_out1), .in(Instruction), .sel(comparator_8_eq));
  Shifter #(.shift("ar"), .width(32)) shifter_4 (.in(demultiplexer_5_out0), .\dist (5'b10100), .out(Immediate));
  assign Immediate = {{27{1'b0}}, demultiplexer_5_out1[24:20]};  // Bit_Extender bit_extender_4

  // Notes on the sheet:
  //   INPUTS to your circuit
  //   DON'T CHANGE THE LOCATIONS OF THE INPUTS AND OUTPUTS!
  //   OUTPUT from your circuit
endmodule
