// Logisim project regfile.circ as structural Verilog: 1 circuit, main circuit regfile
module regfile (
  input  [4:0] ReadIndex1,
  input  [4:0] ReadIndex2,
  input  [4:0] WriteIndex,
  input  [31:0] WriteData,
  input  RegWEn,
  input  clk,
  output [31:0] ra,
  output [31:0] sp,
  output [31:0] t0,
  output [31:0] t1,
  output [31:0] t2,
  output [31:0] s0,
  output [31:0] s1,
  output [31:0] a0,
  output [31:0] ReadData1,
  output [31:0] ReadData2
);

  wire [31:0] a0_t, ra_t, s0_t, s1_t, sp_t, t0_t, t1_t, t2_t, x0T, x3, x3T, x4, x4T, x11, x11T, x12, x12T,
       x13, x13T, x14, x14T, x15, x15T, x16, x16T, x17, x17T, x18, x18T, x19, x19T, x20, x20T, x21, x21T,
       x22, x22T, x23, x23T, x24, x24T, x25, x25T, x26, x26T, x27, x27T, x28, x28T, x29, x29T, x30, x30T,
       x31, x31T;

  Register #(.width(32)) x1 (.D(ra_t), .en(RegWEn), .clk(clk), .Q(ra));  // open: clr
  Register #(.width(32)) x0 (.D({32{1'b0}}), .en(RegWEn), .clk(clk), .Q(x0T));  // open: clr
  Register #(.width(32)) x2 (.D(sp_t), .en(RegWEn), .clk(clk), .Q(sp));  // open: clr
  Register #(.width(32)) u_x3 (.D(x3), .en(RegWEn), .clk(clk), .Q(x3T));  // open: clr
  Register #(.width(32)) u_x4 (.D(x4), .en(RegWEn), .clk(clk), .Q(x4T));  // open: clr
  Register #(.width(32)) x5 (.D(t0_t), .en(RegWEn), .clk(clk), .Q(t0));  // open: clr
  Register #(.width(32)) x6 (.D(t1_t), .en(RegWEn), .clk(clk), .Q(t1));  // open: clr
  Register #(.width(32)) x7 (.D(t2_t), .en(RegWEn), .clk(clk), .Q(t2));  // open: clr
  Register #(.width(32)) x8 (.D(s0_t), .en(RegWEn), .clk(clk), .Q(s0));  // open: clr
  Register #(.width(32)) x9 (.D(s1_t), .en(RegWEn), .clk(clk), .Q(s1));  // open: clr
  Register #(.width(32)) x10 (.D(a0_t), .en(RegWEn), .clk(clk), .Q(a0));  // open: clr
  Register #(.width(32)) u_x11 (.D(x11), .en(RegWEn), .clk(clk), .Q(x11T));  // open: clr
  Register #(.width(32)) u_x12 (.D(x12), .en(RegWEn), .clk(clk), .Q(x12T));  // open: clr
  Register #(.width(32)) u_x13 (.D(x13), .en(RegWEn), .clk(clk), .Q(x13T));  // open: clr
  Register #(.width(32)) u_x14 (.D(x14), .en(RegWEn), .clk(clk), .Q(x14T));  // open: clr
  Register #(.width(32)) u_x15 (.D(x15), .en(RegWEn), .clk(clk), .Q(x15T));  // open: clr
  Register #(.width(32)) u_x16 (.D(x16), .en(RegWEn), .clk(clk), .Q(x16T));  // open: clr
  Register #(.width(32)) u_x18 (.D(x18), .en(RegWEn), .clk(clk), .Q(x18T));  // open: clr
  Register #(.width(32)) u_x19 (.D(x19), .en(RegWEn), .clk(clk), .Q(x19T));  // open: clr
  Register #(.width(32)) u_x20 (.D(x20), .en(RegWEn), .clk(clk), .Q(x20T));  // open: clr
  Register #(.width(32)) u_x21 (.D(x21), .en(RegWEn), .clk(clk), .Q(x21T));  // open: clr
  Register #(.width(32)) u_x17 (.D(x17), .en(RegWEn), .clk(clk), .Q(x17T));  // open: clr
  Register #(.width(32)) u_x22 (.D(x22), .en(RegWEn), .clk(clk), .Q(x22T));  // open: clr
  Register #(.width(32)) u_x23 (.D(x23), .en(RegWEn), .clk(clk), .Q(x23T));  // open: clr
  Register #(.width(32)) u_x24 (.D(x24), .en(RegWEn), .clk(clk), .Q(x24T));  // open: clr
  Register #(.width(32)) u_x25 (.D(x25), .en(RegWEn), .clk(clk), .Q(x25T));  // open: clr
  Register #(.width(32)) u_x26 (.D(x26), .en(RegWEn), .clk(clk), .Q(x26T));  // open: clr
  Register #(.width(32)) u_x27 (.D(x27), .en(RegWEn), .clk(clk), .Q(x27T));  // open: clr
  Register #(.width(32)) u_x28 (.D(x28), .en(RegWEn), .clk(clk), .Q(x28T));  // open: clr
  Register #(.width(32)) u_x29 (.D(x29), .en(RegWEn), .clk(clk), .Q(x29T));  // open: clr
  Register #(.width(32)) u_x30 (.D(x30), .en(RegWEn), .clk(clk), .Q(x30T));  // open: clr
  Register #(.width(32)) u_x31 (.D(x31), .en(RegWEn), .clk(clk), .Q(x31T));  // open: clr
  Demultiplexer #(.select(5), .width(32)) demultiplexer_1 (
    .out1(ra_t), .out2(sp_t), .out3(x3), .out4(x4), .out5(t0_t), .out6(t1_t), .out7(t2_t), .out8(s0_t),
    .out9(s1_t), .out10(a0_t), .out11(x11), .out12(x12), .out13(x13), .out14(x14), .out15(x15), .out16(x16),
    .out17(x17), .out18(x18), .out19(x19), .out20(x20), .out21(x21), .out22(x22), .out23(x23), .out24(x24),
    .out25(x25), .out26(x26), .out27(x27), .out28(x28), .out29(x29), .out30(x30), .out31(x31),
    .in(WriteData), .sel(WriteIndex));  // open: out0
  Multiplexer #(.select(5), .width(32)) multiplexer_1 (
    .in0(x0T), .in1(ra), .in2(sp), .in3(x3T), .in4(x4T), .in5(t0), .in6(t1), .in7(t2), .in8(s0), .in9(s1),
    .in10(a0), .in11(x11T), .in12(x12T), .in13(x13T), .in14(x14T), .in15(x15T), .in16(x16T), .in17(x17T),
    .in18(x18T), .in19(x19T), .in20(x20T), .in21(x21T), .in22(x22T), .in23(x23T), .in24(x24T), .in25(x25T),
    .in26(x26T), .in27(x27T), .in28(x28T), .in29(x29T), .in30(x30T), .in31(x31T), .out(ReadData1),
    .sel(ReadIndex1));
  Multiplexer #(.select(5), .width(32)) multiplexer_2 (
    .in0(x0T), .in1(ra), .in2(sp), .in3(x3T), .in4(x4T), .in5(t0), .in6(t1), .in7(t2), .in8(s0), .in9(s1),
    .in10(a0), .in11(x11T), .in12(x12T), .in13(x13T), .in14(x14T), .in15(x15T), .in16(x16T), .in17(x17T),
    .in18(x18T), .in19(x19T), .in20(x20T), .in21(x21T), .in22(x22T), .in23(x23T), .in24(x24T), .in25(x25T),
    .in26(x26T), .in27(x27T), .in28(x28T), .in29(x29T), .in30(x30T), .in31(x31T), .out(ReadData2),
    .sel(ReadIndex2));

  // Other names for the same wires on the sheet: x1T[31:0] = ra; x2T[31:0] = sp; x5T[31:0] = t0; x6T[31:0] = t1;
  //   x7T[31:0] = t2; x8T[31:0] = s0; x9T[31:0] = s1; x10T[31:0] = a0

  // Notes on the sheet:
  //   INPUTS to your circuit
  //   DON'T CHANGE THE LOCATIONS OF THE INPUTS AND OUTPUTS!
  //   These are DEBUG/TEST outputs from your circuit.
  //   OUTPUTS from your circuit
endmodule
